// Logisim project CPU_group.circ as structural Verilog: 4 circuits, main circuit main
module main (
  input  in_1,
  input  in_2,
  output [15:0] out_3,
  output [15:0] out_4,
  output [15:0] out_5,
  output [3:0] out_6,
  output [15:0] out_7,
  output [15:0] out_8,
  output [15:0] out_9,
  output [2:0] out_10,
  output [15:0] out_11,
  output [2:0] out_12
);

  wire alu_1_b, and_1_out, and_2_out, and_3_out, clock_1_out, control_1_accessmem, control_1_aluused,
       control_1_andor, control_1_bj, control_1_blebne, control_1_halt, control_1_i, control_1_jump,
       control_1_jumpcall, control_1_ls, control_1_rtn, control_1_writereg, control_1_xadd, not_1_out;
  wire [15:0] adder_2_out, bit_extender_1_out, bit_extender_2_out, multiplexer_1_out, multiplexer_2_out,
       multiplexer_5_out, multiplexer_7_out, PC_q, ra_q, ram_2_dout;

  Clock clock_1 (.out(clock_1_out));
  Register #(.width(16)) PC (.D(out_4), .en(1'b1), .Q(PC_q), .clk(and_1_out), .clr(in_1));
  and and_1 (and_1_out, clock_1_out, ~control_1_halt);  // AND_Gate
  RAM #(.addrWidth(16), .asyncread("true"), .dataWidth(16), .databus("bidir"), .\type ("nonvolatile")) ram_1 (
    .addr(PC_q), .clk(and_1_out), .data({out_6, out_8[11:0]}));  // open: we, oe
  Adder #(.width(16)) adder_1 (.a(PC_q), .b(16'h1), .out(out_3));  // open: cin, cout
  Adder #(.width(16)) adder_2 (.a(PC_q), .b(multiplexer_2_out), .out(adder_2_out));  // open: cin, cout
  Multiplexer #(.width(16)) multiplexer_1 (.in0(out_3), .in1(adder_2_out), .out(multiplexer_1_out), .sel(and_2_out));
  Multiplexer #(.width(16)) multiplexer_2 (
    .in0(bit_extender_2_out), .in1(bit_extender_1_out), .out(multiplexer_2_out), .sel(control_1_bj));
  Multiplexer #(.width(16)) multiplexer_3 (.in0(multiplexer_1_out), .in1(ra_q), .out(out_4), .sel(control_1_rtn));
  Register #(.width(16)) ra (.D(out_3), .en(control_1_jumpcall), .Q(ra_q), .clk(and_1_out));  // open: clr
  and and_2 (and_2_out, alu_1_b, control_1_jump);
  assign bit_extender_1_out = {{4{out_8[11]}}, out_8[11:0]};  // Bit_Extender bit_extender_1
  assign bit_extender_2_out = {{10{out_8[5]}}, out_8[5:0]};  // Bit_Extender bit_extender_2
  control control_1 (
    .in_1(out_6), .BJ(control_1_bj), .jump(control_1_jump), .blebne(control_1_blebne),
    .jumpcall(control_1_jumpcall), .ALUused(control_1_aluused), .andor(control_1_andor),
    .Xadd(control_1_xadd), .WriteReg(control_1_writereg), .I(control_1_i), .LS(control_1_ls),
    .accessMEM(control_1_accessmem), .rtn(control_1_rtn), .halt(control_1_halt));
  Multiplexer #(.width(3)) multiplexer_4 (.in0(out_8[5:3]), .in1(out_8[8:6]), .out(out_12), .sel(control_1_i));
  and and_3 (and_3_out, control_1_i, ~control_1_jump);  // AND_Gate
  Multiplexer #(.width(16)) multiplexer_5 (
    .in0(out_11), .in1(bit_extender_2_out), .out(multiplexer_5_out), .sel(and_3_out));
  Multiplexer #(.width(16)) multiplexer_6 (.in0(multiplexer_7_out), .in1(out_5), .out(out_7), .sel(control_1_aluused));
  // registerfile registerfile_1: pin names not known; wires that end beside it: control_1_writereg, out_12, out_7, and_1_out, out_8[8:6], out_8[11:9], in_2, out_9, out_11
  ALU alu_1 (
    .in_1(out_9), .in_2(multiplexer_5_out), .AndOr(control_1_andor), .AddAnd(control_1_xadd),
    .BneBle(control_1_blebne), .outcome(out_5), .b(alu_1_b));
  RAM #(.addrWidth(16), .asyncread("true"), .dataWidth(16)) ram_2 (
    .addr(out_11), .we(control_1_ls), .oe(not_1_out), .clk(and_1_out), .din(out_9), .dout(ram_2_dout));
  not not_1 (not_1_out, control_1_ls);
  Multiplexer #(.width(16)) multiplexer_7 (
    .in0(multiplexer_5_out), .in1(ram_2_dout), .out(multiplexer_7_out), .sel(control_1_accessmem));

  assign out_8[15:12] = out_6;
  assign out_10 = out_8[11:9];
endmodule

module ALU (
  input  [15:0] in_1,
  input  [15:0] in_2,
  input  AndOr,
  input  AddAnd,
  input  BneBle,
  output [15:0] outcome,
  output b
);

  wire comparator_1_eq, comparator_1_lt, not_1_out, not_2_out, or_2_out;
  wire [15:0] adder_1_out, and_1_out, multiplexer_1_out, or_1_out;

  assign and_1_out = in_1 & in_2;  // AND_Gate and_1, 16 bits wide
  assign or_1_out = in_1 | in_2;  // OR_Gate or_1, 16 bits wide
  Adder #(.width(16)) adder_1 (.a(in_1), .b(in_2), .out(adder_1_out));  // open: cin, cout
  Comparator #(.width(16)) comparator_1 (.a(in_1), .b(in_2), .eq(comparator_1_eq), .lt(comparator_1_lt));  // open: gt
  Multiplexer #(.enable("true"), .width(16)) multiplexer_1 (
    .in0(adder_1_out), .in1(and_1_out), .out(multiplexer_1_out), .sel(AddAnd), .en(1'b1));
  not not_1 (not_1_out, comparator_1_eq);
  or or_2 (or_2_out, comparator_1_eq, comparator_1_lt);
  Multiplexer #(.enable("true"), .width(16)) multiplexer_2 (
    .in0(multiplexer_1_out), .in1(or_1_out), .out(outcome), .sel(AndOr), .en(1'b1));
  Multiplexer multiplexer_3 (.in0(not_1_out), .in1(or_2_out), .out(b), .sel(not_2_out));
  not not_2 (not_2_out, BneBle);
endmodule

module control (
  input  [3:0] in_1,
  output BJ,
  output jump,
  output blebne,
  output jumpcall,
  output ALUused,
  output andor,
  output Xadd,
  output WriteReg,
  output I,
  output LS,
  output accessMEM,
  output rtn,
  output halt
);

  wire and_2_out, and_5_out, and_8_out, and_10_out, not_1_out, not_2_out, or_1_out;

  not not_1 (not_1_out, in_1[3]);
  and and_1 (accessMEM, in_1[1], in_1[2], not_1_out);
  and and_2 (and_2_out, ~in_1[1], in_1[2], not_1_out);  // AND_Gate
  and and_3 (jump, in_1[2], in_1[3]);
  and and_4 (LS, in_1[0], accessMEM);
  or or_1 (or_1_out, in_1[0], in_1[1]);
  not not_2 (not_2_out, in_1[2]);
  and and_5 (and_5_out, ~in_1[0], accessMEM);  // AND_Gate
  and and_6 (rtn, in_1[0], and_2_out);
  and and_7 (halt, ~in_1[0], and_2_out);  // AND_Gate
  and and_8 (and_8_out, jump, ~in_1[1]);  // AND_Gate
  and and_9 (BJ, jump, in_1[1]);
  and and_10 (and_10_out, or_1_out, not_2_out);
  and and_11 (jumpcall, BJ, in_1[0]);
  and and_12 (Xadd, in_1[1], and_10_out);
  or or_2 (WriteReg, ~in_1[2], and_5_out);  // OR_Gate
  and and_13 (blebne, in_1[0], and_8_out);
  and and_14 (andor, in_1[0], Xadd);
  or or_3 (ALUused, and_8_out, and_10_out);

  assign I = in_1[3];
endmodule

module registerfile (
  input  Write,
  input  [2:0] WriteReg,
  input  [15:0] WriteData,
  input  clock,
  input  [2:0] ReadReg2,
  input  [2:0] ReadReg1,
  input  in_7,
  output [15:0] Data1,
  output [15:0] Data2
);

  wire and_1_out, and_2_out, and_3_out, and_4_out, and_5_out, and_6_out, and_7_out, and_8_out,
       decoder_1_out0, decoder_1_out1, decoder_1_out2, decoder_1_out3, decoder_1_out4, decoder_1_out5,
       decoder_1_out6, decoder_1_out7;
  wire [15:0] register_1_q, register_2_q, register_3_q, register_4_q, register_5_q, register_6_q,
       register_7_q, register_8_q;

  Decoder #(.select(3)) decoder_1 (
    .out0(decoder_1_out0), .out1(decoder_1_out1), .out2(decoder_1_out2), .out3(decoder_1_out3),
    .out4(decoder_1_out4), .out5(decoder_1_out5), .out6(decoder_1_out6), .out7(decoder_1_out7),
    .sel(WriteReg), .en(1'b1));
  and and_1 (and_1_out, Write, decoder_1_out0);
  and and_2 (and_2_out, Write, decoder_1_out1);
  and and_3 (and_3_out, Write, decoder_1_out2);
  and and_4 (and_4_out, Write, decoder_1_out3);
  and and_5 (and_5_out, Write, decoder_1_out4);
  and and_6 (and_6_out, Write, decoder_1_out5);
  and and_7 (and_7_out, Write, decoder_1_out6);
  and and_8 (and_8_out, Write, decoder_1_out7);
  Register #(.width(16)) register_1 (.D(WriteData), .en(and_1_out), .Q(register_1_q), .clk(clock), .clr(in_7));
  Register #(.width(16)) register_2 (.D(WriteData), .en(and_2_out), .Q(register_2_q), .clk(clock), .clr(in_7));
  Register #(.width(16)) register_3 (.D(WriteData), .en(and_3_out), .Q(register_3_q), .clk(clock), .clr(in_7));
  Register #(.width(16)) register_4 (.D(WriteData), .en(and_4_out), .Q(register_4_q), .clk(clock), .clr(in_7));
  Register #(.width(16)) register_5 (.D(WriteData), .en(and_5_out), .Q(register_5_q), .clk(clock), .clr(in_7));
  Register #(.width(16)) register_6 (.D(WriteData), .en(and_6_out), .Q(register_6_q), .clk(clock), .clr(in_7));
  Register #(.width(16)) register_7 (.D(WriteData), .en(and_7_out), .Q(register_7_q), .clk(clock), .clr(in_7));
  Register #(.width(16)) register_8 (.D(WriteData), .en(and_8_out), .Q(register_8_q), .clk(clock), .clr(in_7));
  Multiplexer #(.enable("true"), .select(3), .width(16)) multiplexer_1 (
    .in0(register_1_q), .in1(register_2_q), .in2(register_3_q), .in3(register_4_q), .in4(register_5_q),
    .in5(register_6_q), .in6(register_7_q), .in7(register_8_q), .out(Data1), .sel(ReadReg1), .en(1'b1));
  Multiplexer #(.enable("true"), .select(3), .width(16)) multiplexer_2 (
    .in0(register_1_q), .in1(register_2_q), .in2(register_3_q), .in3(register_4_q), .in4(register_5_q),
    .in5(register_6_q), .in6(register_7_q), .in7(register_8_q), .out(Data2), .sel(ReadReg2), .en(1'b1));

  // Notes on the sheet:
  //   clock
endmodule
